// Digital circuit UTS_1_6.dig as structural Verilog
module UTS_1_6 (
  input  A,
  input  B,
  input  C,
  input  D,
  output x
);

  wire and_1_out, and_2_out, and_3_out, and_4_out, not_1_out, not_2_out, not_3_out, not_4_out, not_5_out;

  not not_1 (not_1_out, B);
  not not_2 (not_2_out, C);
  and and_1 (and_1_out, not_3_out, not_1_out, C);
  not not_3 (not_3_out, A);
  and and_2 (and_2_out, not_4_out, not_2_out, D);
  not not_4 (not_4_out, A);
  and and_3 (and_3_out, not_5_out, B, C);
  not not_5 (not_5_out, A);
  and and_4 (and_4_out, A, B, D);
  or or_1 (x, and_1_out, and_2_out, and_3_out, and_4_out);

  // Notes on the sheet:
  //   Indah Nurbaiti 213050012 TKM.21.A
  //   A'B'C + A'C'D + A'BC + ABD
endmodule
