// Digital circuit UTS_1_7.dig as structural Verilog
module UTS_1_7 (
  input  X,
  input  Y,
  input  Z,
  input  W,
  output A
);

  wire and_1_out, and_2_out, and_3_out, and_4_out, not_1_out, not_2_out, not_3_out, not_4_out;

  not not_1 (not_1_out, W);
  not not_2 (not_2_out, X);
  not not_3 (not_3_out, Y);
  not not_4 (not_4_out, W);
  and and_1 (and_1_out, not_1_out, not_2_out, Z);
  and and_2 (and_2_out, X, not_3_out);
  and and_3 (and_3_out, not_4_out, X);
  and and_4 (and_4_out, W, X, Y);
  or or_1 (A, and_1_out, and_2_out, and_3_out, and_4_out);

  // Notes on the sheet:
  //   Indah Nurbaiti 213050012 TKM.21.A
  //   W'X'Z + XY' + W'X + WXY
endmodule
